# Fritzing sketch robot-head (saved by Fritzing 0.9.6b)
breadboards: 2

parts:
  U1 = NodeMCU V3.0
  LED1 = LED - 5mm [color="Green (565nm)" current=0.030 package="5 mm [THT]"]
  LED2 = LED - 5mm [color="Green (565nm)" current=0.030 package="5 mm [THT]"]
  LED3 = LED - 5mm [color="Green (565nm)" current=0.030 package="5 mm [THT]"]
  LED4 = LED - 5mm [color="Yellow (595nm)" current=0.030 package="5 mm [THT]"]
  LED5 = LED - 5mm [color="Yellow (595nm)" current=0.030 package="5 mm [THT]"]
  R1 = Resistor [tolerance=±5% power=0.25 resistance=220 package=THT]
  R2 = Resistor [tolerance=±5% power=0.25 resistance=220 package=THT]
  R3 = Resistor [tolerance=±5% power=0.25 resistance=220 package=THT]
  R4 = Resistor [tolerance=±5% power=0.25 resistance=220 package=THT]
  R5 = Resistor [tolerance=±5% power=0.25 resistance=220 package=THT]
  U2 = 74HC595 [package="DIP16 [THT]"]
  LCD1 = TFT 1.8 inch 160x128 w SD
  R6 = Resistor [tolerance=±5% power=0.25 resistance=22 package=THT]

nets:
  N1: U1.D0, LCD1.pin_9
  N2: U1.D1, U2.SH_CP
  N3: U1.D2, U2.ST_CP
  N4: U1.D3, U2.DS
  N5: U1.D4, LCD1.pin_5
  N6: U1.GND#6, U1.GND#13, U1.GND#16, U1.GND#33, LED1.cathode, LED2.cathode, LED3.cathode, LED4.cathode, LED5.cathode, U2.GND, U2.OE, LCD1.pin2
  N7: U1.D5, LCD1.pin_7, LCD1.pin_12
  N8: U1.D6, LCD1.pin_11
  N9: U1.D7, LCD1.pin_6, LCD1.pin_10
  N10: U1.D8, LCD1.pin3
  VIN: U1.Vin, U2.MR, U2.VCC, LCD1.pin_1
  N11: U1.RST, LCD1.pin4
  N12: U1.S3, R6.Pin_0
  N13: LED1.anode, R2.Pin_0
  N14: LED2.anode, R1.Pin_0
  N15: LED3.anode, R3.Pin_0
  N16: LED4.anode, R4.Pin_0
  N17: LED5.anode, R5.Pin_0
  N18: R1.Pin_1, U2.Q2
  N19: R2.Pin_1, U2.Q1
  N20: R3.Pin_1, U2.Q3
  N21: R4.Pin_1, U2.Q4
  N22: R5.Pin_1, U2.Q5
  N23: LCD1.pin_8, R6.Pin_1

custom parts:
  NodeMCU V3.0: ESP8266 based NodeMCU
  TFT 1.8 inch 160x128 w SD: This is a generic 1.8 tft spi lcd display available on ebay and others. The 1.8" display has 128x160 color pixels.
