# Fritzing sketch stromzaehler_breadboard (saved by Fritzing 0.9.6b)
breadboards: 1

parts:
  WeMos_D1_Mini1 = WeMos D1 Mini
  J1 = female pin header, 4 pins [form="♀ (female)"]
  J2 = female pin header, 4 pins [form="♀ (female)"]
  LED1 = LED - 5mm [color="Red (633nm)" current=0.030 package="5 mm [THT]"]
  LED2 = LED - 5mm [color="Red (633nm)" current=0.030 package="5 mm [THT]"]
  R1 = Resistor [tolerance=±5% power=0.25 resistance=100 package=THT]
  R2 = Resistor [tolerance=±5% power=0.25 resistance=100 package=THT]
  S1 = Pushbutton [package="[THT]"]
  BATT1 = 4xAA Switchable Battery Pack w/Bare Wire

nets:
  N1: WeMos_D1_Mini1.5V, BATT1.POS
  N2: WeMos_D1_Mini1.D0, WeMos_D1_Mini1.RST
  N3: WeMos_D1_Mini1.D1, J1.pin2
  N4: WeMos_D1_Mini1.D2, J1.pin3
  N5: WeMos_D1_Mini1.D5, J2.pin3
  N6: WeMos_D1_Mini1.D6, J2.pin2
  N7: WeMos_D1_Mini1.D7, R2.Pin_0, S1.Pin_1, S1.Pin_2
  N8: WeMos_D1_Mini1.D8, R1.Pin_1, S1.Pin_3, S1.Pin_4
  N9: WeMos_D1_Mini1.G, J1.pin1, J2.pin1, LED1.cathode, LED2.cathode, BATT1.NEG
  N10: LED1.anode, R2.Pin_1
  N11: LED2.anode, R1.Pin_0

custom parts:
  WeMos D1 Mini: The D1 mini is a mini wifi board based on ESP-8266EX.
  4xAA Switchable Battery Pack w/Bare Wire: 4xAA Switchable Battery Pack with Bare Wire connection
